# Fritzing sketch 1 led and 1 switch (saved by Fritzing 0.7.5b)
breadboards: 1

parts:
  RaspberryPi1 = Raspberry Pi Model B
  LED1 = LED - 3mm [color="Red (633nm)" package="3 mm [THT]"]
  R2 = Resistor [tolerance=±5% resistance=220 package=THT]
  S1 = Pushbutton [package="[THT]"]

nets:
  N1: RaspberryPi1.GND, LED1.cathode, S1.Pin_1, S1.Pin_2
  N2: RaspberryPi1.TXD, S1.Pin_3, S1.Pin_4
  N3: RaspberryPi1.RXD, R2.Pin_1
  N4: LED1.anode, R2.Pin_0

custom parts:
  Raspberry Pi Model B: Raspberry Pi (Model B)
