# Fritzing sketch 1button (saved by Fritzing 0.7.5b)
breadboards: 1

parts:
  Raspberry_Pi_B_rev1 = Raspberry Pi B rev2
  S2 = Pushbutton [package="[THT]"]

nets:
  N1: Raspberry_Pi_B_rev1.GND, S2.Pin_1, S2.Pin_2
  N2: Raspberry_Pi_B_rev1.GPIO_23, S2.Pin_3, S2.Pin_4

custom parts:
  Raspberry Pi B rev2: The awesome Raspberry Pi ARM Board
