# Fritzing sketch 1led1button (saved by Fritzing 0.8.5b)
breadboards: 1

parts:
  LED1 = LED - 3mm [color="Red (633nm)" package="3 mm [THT]"]
  S1 = Pushbutton [package="[THT]"]
  Raspberry_Pi_B_rev1 = Raspberry Pi B rev2
  R3 = 560 Ω Resistor [package=THT]

nets:
  N1: LED1.cathode, S1.Pin_1, S1.Pin_2, Raspberry_Pi_B_rev1.GND
  N2: LED1.anode, R3.Pin_1
  N3: S1.Pin_3, S1.Pin_4, Raspberry_Pi_B_rev1.GPIO_14
  N4: Raspberry_Pi_B_rev1.GPIO_15, Raspberry_Pi_B_rev1.GPIO_18, R3.Pin_0

custom parts:
  Raspberry Pi B rev2: The awesome Raspberry Pi ARM Board
  560 Ω Resistor: A generic resistor (0.25W)
