# Fritzing sketch 1ledbasic (saved by Fritzing 0.7.5b)
breadboards: 1

parts:
  LED1 = LED - 3mm [color="Red (633nm)" package="3 mm [THT]"]
  Raspberry_Pi_B_rev1 = Raspberry Pi B rev2
  R4 = 560 Ω Resistor [package=THT]

nets:
  N1: LED1.cathode, Raspberry_Pi_B_rev1.GND
  N2: LED1.anode, R4.Pin_1
  N3: Raspberry_Pi_B_rev1.3V3, R4.Pin_0

custom parts:
  Raspberry Pi B rev2: The awesome Raspberry Pi ARM Board
  560 Ω Resistor: A generic resistor (0.25W)
