# Fritzing sketch 2button (saved by Fritzing 0.8.5b)
breadboards: 1

parts:
  S1 = Pushbutton [package="[THT]"]
  S2 = Pushbutton [package="[THT]"]
  Raspberry_Pi_B_rev1 = Raspberry Pi B rev2

nets:
  N1: S1.Pin_1, S2.Pin_1, S2.Pin_2, Raspberry_Pi_B_rev1.GND
  N2: S2.Pin_3, S2.Pin_4

custom parts:
  Raspberry Pi B rev2: The awesome Raspberry Pi ARM Board
