# Fritzing sketch 3 led and 1 switch (saved by Fritzing 0.7.5b)
breadboards: 1

parts:
  RaspberryPi1 = Raspberry Pi Model B
  LED1 = LED - 3mm [color="Red (633nm)" package="3 mm [THT]"]
  R2 = Resistor [tolerance=±5% resistance=220 package=THT]
  R3 = Resistor [tolerance=±5% resistance=220 package=THT]
  LED2 = LED - 3mm [color="Orange (620nm)" package="3 mm [THT]"]
  LED3 = LED - 3mm [color="Green (560nm)" package="3 mm [THT]"]
  R4 = Resistor [tolerance=±5% resistance=220 package=THT]
  S1 = Pushbutton [package="[THT]"]

nets:
  N1: RaspberryPi1.GND, LED1.cathode, LED2.cathode, LED3.cathode, S1.Pin_1, S1.Pin_2
  N2: RaspberryPi1.TXD, S1.Pin_3, S1.Pin_4
  N3: RaspberryPi1.RXD, R2.Pin_1
  N4: RaspberryPi1.#18, R3.Pin_1
  N5: RaspberryPi1.#23, R4.Pin_1
  N6: LED1.anode, R2.Pin_0
  N7: R3.Pin_0, LED2.anode
  N8: LED3.anode, R4.Pin_0

custom parts:
  Raspberry Pi Model B: Raspberry Pi (Model B)
