# Fritzing sketch 3 led and 3 switch (saved by Fritzing 0.7.5b)
breadboards: 1

parts:
  RaspberryPi1 = Raspberry Pi Model B
  LED1 = LED - 3mm [color="Red (633nm)" package="3 mm [THT]"]
  R2 = Resistor [tolerance=±5% resistance=220 package=THT]
  S1 = Pushbutton [package="[THT]"]
  LED2 = LED - 3mm [color="Red (633nm)" package="3 mm [THT]"]
  R3 = Resistor [tolerance=±5% resistance=220 package=THT]
  S2 = Pushbutton [package="[THT]"]
  LED3 = LED - 3mm [color="Red (633nm)" package="3 mm [THT]"]
  R4 = Resistor [tolerance=±5% resistance=220 package=THT]
  S3 = Pushbutton [package="[THT]"]

nets:
  N1: RaspberryPi1.GND, LED1.cathode, S1.Pin_3, S1.Pin_4, LED2.cathode, S2.Pin_3, S2.Pin_4, LED3.cathode, S3.Pin_3, S3.Pin_4
  N2: RaspberryPi1.TXD, S1.Pin_1, S1.Pin_2
  N3: RaspberryPi1.RXD, R2.Pin_1
  N4: RaspberryPi1.#18, S3.Pin_1, S3.Pin_2
  N5: RaspberryPi1.#23, R4.Pin_1
  N6: RaspberryPi1.#24, S2.Pin_1, S2.Pin_2
  N7: RaspberryPi1.#25, R3.Pin_1
  N8: LED1.anode, R2.Pin_0
  N9: LED2.anode, R3.Pin_0
  N10: LED3.anode, R4.Pin_0

custom parts:
  Raspberry Pi Model B: Raspberry Pi (Model B)
