# Fritzing sketch 3led1button (saved by Fritzing 0.8.5b)
breadboards: 1

parts:
  LED1 = LED - 3mm [color="Red (633nm)" package="3 mm [THT]"]
  LED2 = LED - 3mm [color="Orange (620nm)" package="3 mm [THT]"]
  LED3 = LED - 3mm [color="Green (560nm)" package="3 mm [THT]"]
  S1 = Pushbutton [package="[THT]"]
  Raspberry_Pi_B_rev1 = Raspberry Pi B rev2
  R5 = 560 Ω Resistor [package=THT]
  R6 = 560 Ω Resistor [package=THT]
  R7 = 560 Ω Resistor [package=THT]

nets:
  N1: LED1.cathode, LED2.cathode, LED3.cathode, S1.Pin_1, S1.Pin_2, Raspberry_Pi_B_rev1.GND
  N2: LED1.anode, R7.Pin_1
  N3: LED2.anode, R6.Pin_1
  N4: LED3.anode, R5.Pin_1
  N5: S1.Pin_3, S1.Pin_4, Raspberry_Pi_B_rev1.GPIO_14
  N6: Raspberry_Pi_B_rev1.GPIO_23, R5.Pin_0
  N7: Raspberry_Pi_B_rev1.GPIO_15, R7.Pin_0
  N8: Raspberry_Pi_B_rev1.GPIO_18, R6.Pin_0

custom parts:
  Raspberry Pi B rev2: The awesome Raspberry Pi ARM Board
  560 Ω Resistor: A generic resistor (0.25W)
