# Fritzing sketch STUR-1 led and 1 switch (saved by Fritzing 0.8.5b)
breadboards: 1

parts:
  LED1 = LED - 3mm [color="Red (633nm)" package="3 mm [THT]"]
  R2 = Resistor [tolerance=±5% resistance=220 package=THT]
  S1 = Pushbutton [package="[THT]"]
  Raspberry_Pi_B_rev1 = Raspberry Pi B rev2

nets:
  N1: LED1.anode, R2.Pin_0
  N2: S1.Pin_1, S1.Pin_2, Raspberry_Pi_B_rev1.GND
  N3: S1.Pin_3, S1.Pin_4, Raspberry_Pi_B_rev1.GPIO_14
  N4: Raspberry_Pi_B_rev1.GPIO_15, Raspberry_Pi_B_rev1.GPIO_18

custom parts:
  Raspberry Pi B rev2: The awesome Raspberry Pi ARM Board
