# Fritzing sketch STUR-2leds (saved by Fritzing 0.8.5b)
breadboards: 1

parts:
  LED1 = LED - 3mm [color="Red (633nm)" package="3 mm [THT]"]
  LED2 = LED - 3mm [color="Red (633nm)" package="3 mm [THT]"]
  Raspberry_Pi_B_rev1 = Raspberry Pi B rev2
  R4 = 560 Ω Resistor [package=THT]
  R5 = 560 Ω Resistor [package=THT]

nets:
  N1: LED1.cathode, LED2.cathode, Raspberry_Pi_B_rev1.GND
  N2: LED1.anode, R4.Pin_1
  N3: LED2.anode, R5.Pin_1
  N4: Raspberry_Pi_B_rev1.GPIO_14, R4.Pin_0
  N5: Raspberry_Pi_B_rev1.GPIO_15, R5.Pin_0

custom parts:
  Raspberry Pi B rev2: The awesome Raspberry Pi ARM Board
  560 Ω Resistor: A generic resistor (0.25W)
