# Fritzing sketch breadboard (saved by Fritzing 0.7.5b)
breadboards: 1

parts:
  LED1 = LED - 3mm [color="Red (633nm)" package="3 mm [THT]"]
  R3 = 560 Ω Resistor [package=THT]

nets:
  N1: LED1.anode, R3.Pin_1

custom parts:
  560 Ω Resistor: A generic resistor (0.25W)
